# Fritzing sketch human_following_robot (saved by Fritzing 0.9.3b)

parts:
  Part2 = AF_mshield-v1.2_breadboard
  M1 = Getriebemotor
  M2 = Getriebemotor
  M3 = Getriebemotor
  M4 = Getriebemotor
  M5 = fc-51 [package=THT]
  M6 = fc-51 [package=THT]
  J2 = micro USB connector MK5P [package=usb-microb]
  Part3 = USB Type A Female Breakout Board [part_number=BOB-12700]
  Mod1 = 2S-BMS
  BAT1 = 18650 battery holder [package=battery-18650-kit]
  BAT2 = 18650 battery holder [package=battery-18650-kit]
  Part1 = Arduino Uno (Rev3)  # not connected
  hc-sr1 = hc-sr04
  USBTTL1 = USB A Plug
  USBTTL2 = Micro USB B Plug
  J3 = Basic Servo
  Mod2 = lithium-battery-indicator
  U1 = SWITCH-SPST-2 [package=switch-spst-vertical]

nets:
  N1: Part2.V+, Mod2.pin1, U1.O
  GND: Part2.GND, M5.pin2, M6.pin2, Part3.GND, hc-sr1.GND, J3.gnd, Mod2.pin2
  N2: Part2.1, hc-sr1.Echo
  N3: Part2.2, hc-sr1.Trig
  N4: Part2.3, M5.pin1
  N5: Part2.4, M6.pin1
  VCC: Part2.VCC, M5.pin3, M6.pin3, hc-sr1.VCC, J3.vcc
  N6: Part2.PWM1B, J3.pulse
  N7: Part2.P1#166, M4.pin_2
  N8: Part2.P2#167, M4.pin_1
  N9: Part2.P4#169, M1.pin_2
  N10: Part2.P5#170, M1.pin_1
  N11: Part2.P1#171, M2.pin_2
  N12: Part2.P2#172, M2.pin_1
  N13: Part2.P4#174, M3.pin_2
  N14: Part2.P5#175, M3.pin_1
  N15: J2.VCC, Mod1.pin3#3
  N16: J2.GND, Mod1.pin3#2
  N17: Part3.VCC, U1.P
  N18: Mod1.pin1, BAT1.-
  N19: Mod1.pin2, BAT2.+
  N20: Mod1.pin3#4, BAT1.+, BAT2.-
  N21: USBTTL1.usb, USBTTL2.usb

notes:
  The L293D Arduino Motor Driver is a hat for Arduino UNO

custom parts:
  : motor Shield v1 Adafruit Adafruit Motor/Stepper/Servo Shield for Arduino kit [v1.2] : ID 81 : $19.50 : Adafruit Industries, Unique & fun DIY electronics and kits
  micro USB connector MK5P: micro USB connector which only uses holes no slots. Apparently a standard of some kind called MK5P. Note the text in pcb that marks the edge of the board (and the amount the connector protudes) will both be truncated from the final board if aligned correctly.
  USB Type A Female Breakout Board: USB breakout board for a Type A connector. sparkfun.com
  2S-BMS: 2S-BMS LIPO battery charger / protection unit. Note pcb does not match the board as it will likely connect with wires, so pcb is 5 pads suitable for .1in header pins.
  18650 battery holder: 18650 Battery
  USB A Plug: USB A Plug breadboard only for documetnation purposes.
  lithium-battery-indicator: Lithium battery charge indicator.
